# Fritzing sketch dice_layout (saved by Fritzing 0.9.4)
breadboards: 2

parts:
  Argon1 = Particle Argon
  LED1 = LED - 3mm [color="Red (633nm)" package="3 mm [THT]"]
  LED4 = LED - 3mm [color="Red (633nm)" package="3 mm [THT]"]
  LED5 = LED - 3mm [color="Red (633nm)" package="3 mm [THT]"]
  R1 = Resistor [tolerance=±5% resistance=330 package=THT]
  R2 = Resistor [tolerance=±5% resistance=330 package=THT]
  R3 = Resistor [tolerance=±5% resistance=330 package=THT]
  LED6 = LED - 3mm [color="Red (633nm)" package="3 mm [THT]"]
  LED7 = LED - 3mm [color="Red (633nm)" package="3 mm [THT]"]
  LED8 = LED - 3mm [color="Red (633nm)" package="3 mm [THT]"]
  R4 = Resistor [tolerance=±5% resistance=330 package=THT]
  R5 = Resistor [tolerance=±5% resistance=330 package=THT]
  R6 = Resistor [tolerance=±5% resistance=330 package=THT]
  LED9 = LED - 3mm [color="Red (633nm)" package="3 mm [THT]"]
  LED10 = LED - 3mm [color="Red (633nm)" package="3 mm [THT]"]
  LED11 = LED - 3mm [color="Red (633nm)" package="3 mm [THT]"]
  R7 = Resistor [tolerance=±5% resistance=330 package=THT]
  R8 = Resistor [tolerance=±5% resistance=330 package=THT]
  R9 = Resistor [tolerance=±5% resistance=330 package=THT]

nets:
  N1: Argon1.GND, LED1.cathode, LED4.cathode, LED6.cathode, LED7.cathode, LED9.cathode, LED10.cathode, LED11.cathode
  N2: Argon1.A0, R2.Pin_1
  N3: Argon1.A1, R1.Pin_1
  N4: Argon1.D2, R8.Pin_1
  N5: Argon1.D3, R9.Pin_1
  N6: Argon1.D4, R7.Pin_1
  N7: Argon1.D5, R6.Pin_1
  N8: Argon1.D6, R5.Pin_1
  N9: Argon1.D7, R4.Pin_1
  N10: Argon1.D8, R3.Pin_1
  N11: LED1.anode, R3.Pin_0
  N12: LED4.anode, R2.Pin_0
  N13: LED5.anode, R1.Pin_0
  N14: LED6.anode, R4.Pin_0
  N15: LED7.anode, R6.Pin_0
  N16: LED8.anode, R5.Pin_0
  N17: LED9.anode, R8.Pin_0
  N18: LED10.anode, R9.Pin_0
  N19: LED11.anode, R7.Pin_0

custom parts:
  Particle Argon: The Argon is a powerful Wi-Fi enabled development board that can act as either a standalone Wi-Fi endpoint or Wi-Fi enabled gateway for Particle Mesh networks. It is based on the Nordic nRF52840 and has built-in battery charging circuitry so it’s easy to connect a Li-Po and deploy your local network in minutes. The Argon is great for connecting existing projects to the Particle Device Cloud or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
