# Fritzing sketch switch (saved by Fritzing 0.9.4)
breadboards: 1

parts:
  R2 = Resistor [tolerance=±5% resistance=330 package=THT]  # not connected
  R3 = Resistor [tolerance=±5% resistance=330 package=THT]  # not connected
  S1 = Toggle Switch [package=THT]
  A1 = Particle Photon 2

nets:
  N1: S1.L1, A1.Pin_2, A1.Pin_31
  N2: S1.COM, A1.Pin_10
  N3: S1.L2, A1.Pin_4, A1.Pin_30
  N4: A1.Pin_28, A1.Pin_29

custom parts:
  Particle Photon 2: The Photon 2 is a development module with a microcontroller and Wi-Fi networking. -- This Fritzing file originally created by Peter Van Epp https://forum.fritzing.org/t/request-particle-photon2/19824/2 5/18/2024 - Rob Parke Rotated breadboard image
