# Fritzing sketch etch-a-sketch (saved by Fritzing 0.9.10b)
breadboards: 1

parts:
  Part1 = OLED Monochrome 128x64 1.3 inch [part_number=938]
  R2 = TRIMPOT [maximum_resistance=10kΩ knob_status=50% power=0.5W package=3362u-2]
  R3 = TRIMPOT [maximum_resistance=10kΩ knob_status=50% power=0.5W package=3362u-2]
  A1 = Particle Photon 2
  S1 = Pushbutton [package="[THT]"]
  R4 = Resistor [tolerance=±5% resistance=10k package="1206 [SMD]"]

nets:
  N1: Part1.MOSI_SDA, A1.Pin_12
  N2: Part1.SCLK_SCK, A1.Pin_11
  N3: Part1.DC_SA0, A1.Pin_22
  N4: Part1.RESET, A1.Pin_23
  N5: Part1.CS, A1.Pin_24
  N6: Part1.3.3V, R2.CW, R3.CW, A1.Pin_2, A1.Pin_31, R4.Pin_1
  N7: Part1.GND, R2.CCW, R3.CCW, A1.Pin_4, A1.Pin_30, S1.Pin_1, S1.Pin_2
  N8: R2.WIPER, A1.Pin_5
  N9: R3.WIPER, A1.Pin_6
  N10: A1.Pin_19, S1.Pin_3, S1.Pin_4, R4.Pin_0
  N11: A1.Pin_28, A1.Pin_29

notes:
  Pin layout shown might be different from your OLED

custom parts:
  OLED Monochrome 128x64 1.3 inch: These displays are small, only about 1.3" diagonal, but very readable due to the high contrast of an OLED display. This display is made of 128x64 individual white OLED pixels, each one is turned on or off by the controller chip. Because the display makes its own light, no backlight is required. This reduces the power required to run the OLED and is why the display has such high contrast; we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
  Particle Photon 2: The Photon 2 is a development module with a microcontroller and Wi-Fi networking. -- This Fritzing file originally created by Peter Van Epp https://forum.fritzing.org/t/request-particle-photon2/19824/2 5/18/2024 - Rob Parke Rotated breadboard image
