# Fritzing sketch etch-a-sketch_v2 (saved by Fritzing 0.9.10b)
breadboards: 1

parts:
  S1 = Pushbutton [package="[THT]"]
  R1 = Resistor [tolerance=±5% resistance=10k power=0.25 package=THT]
  R2 = TRIMPOT [maximum_resistance=10kΩ knob_status=50% power=0.5W package=3362u-2]
  R3 = TRIMPOT [maximum_resistance=10kΩ knob_status=50% power=0.5W package=3362u-2]
  Qwiic_OLED_Breakout2 = Qwiic_OLED_Breakout  # not connected
  A1 = Particle Photon 2

nets:
  N1: S1.Pin_1, S1.Pin_2, R2.CCW, R3.CCW, A1.Pin_4, A1.Pin_30
  N2: S1.Pin_3, S1.Pin_4, R1.Pin_0, A1.Pin_19
  N3: R1.Pin_1, R2.CW, R3.CW, A1.Pin_2
  N4: R2.WIPER, A1.Pin_6
  N5: R3.WIPER, A1.Pin_5
  N6: A1.Pin_28, A1.Pin_29

notes:
  OLED
  Use Qwiic cable

custom parts:
  Qwiic_OLED_Breakout: The SparkFun Qwiic Micro OLED Breakout is a Qwiic-enabled version of our popular Micro OLED display! The small monochrome, blue-on-black OLED screen presents incredibly clear images for your viewing pleasure. It’s “micro,” but it still packs a punch --- the OLED display is crisp, and you can fit a deceivingly large amount of graphics on there. This breakout is perfect for adding graphics to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
  Particle Photon 2: The Photon 2 is a development module with a microcontroller and Wi-Fi networking. -- This Fritzing file originally created by Peter Van Epp https://forum.fritzing.org/t/request-particle-photon2/19824/2 5/18/2024 - Rob Parke Rotated breadboard image
