# Fritzing sketch etch-a-sketch (saved by Fritzing 0.9.3b)
breadboards: 1

parts:
  Part1 = OLED Monochrome 128x64 1.3 inch [part_number=938]
  Argon1 = Particle Argon
  S1 = Pushbutton [package="[THT]"]
  R1 = Resistor [tolerance=±5% resistance=220 package=THT]

nets:
  N1: Part1.MOSI_SDA, Argon1.MO
  N2: Part1.SCLK_SCK, Argon1.SCK
  N3: Part1.DC_SA0, Argon1.D5
  N4: Part1.RESET, Argon1.D6
  N5: Part1.CS, Argon1.D4
  3.3V: Part1.3.3V, Argon1.3.3V, R1.Pin_1
  GND: Part1.GND, Argon1.GND, S1.Pin_1, S1.Pin_2
  N6: Argon1.D2, S1.Pin_3, S1.Pin_4, R1.Pin_0

custom parts:
  OLED Monochrome 128x64 1.3 inch: These displays are small, only about 1.3" diagonal, but very readable due to the high contrast of an OLED display. This display is made of 128x64 individual white OLED pixels, each one is turned on or off by the controller chip. Because the display makes its own light, no backlight is required. This reduces the power required to run the OLED and is why the display has such high contrast; we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
  Particle Argon: The Argon is a powerful Wi-Fi enabled development board that can act as either a standalone Wi-Fi endpoint or Wi-Fi enabled gateway for Particle Mesh networks. It is based on the Nordic nRF52840 and has built-in battery charging circuitry so it’s easy to connect a Li-Po and deploy your local network in minutes. The Argon is great for connecting existing projects to the Particle Device Cloud or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
