# Fritzing sketch switch-magnetic-door (saved by Fritzing 0.9.3b)
breadboards: 1

parts:
  S3 = Magnetic Door Switch [package=reed_switch_plastic]
  Argon2 = Particle Argon
  LED2 = LED - 5mm [color="Red (633nm)" package="5 mm [THT]"]
  R1 = Resistor [tolerance=±5% resistance=330 package=THT]
  R2 = Resistor [tolerance=±5% resistance=10k package=THT]

nets:
  N1: S3.1, Argon2.D2, R2.Pin_1
  N2: S3.2, Argon2.GND, R1.Pin_0
  N3: Argon2.3.3V, R2.Pin_0
  N4: Argon2.D3, LED2.anode
  N5: LED2.cathode, R1.Pin_1

custom parts:
  Particle Argon: The Argon is a powerful Wi-Fi enabled development board that can act as either a standalone Wi-Fi endpoint or Wi-Fi enabled gateway for Particle Mesh networks. It is based on the Nordic nRF52840 and has built-in battery charging circuitry so it’s easy to connect a Li-Po and deploy your local network in minutes. The Argon is great for connecting existing projects to the Particle Device Cloud or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
