# Fritzing sketch washer_switch-magnetic-door_and_rgb_led (saved by Fritzing 0.9.4)
breadboards: 1

parts:
  R6 = Resistor [tolerance=±5% resistance=330 package=THT]
  R7 = Resistor [tolerance=±5% resistance=330 package=THT]
  R8 = Resistor [tolerance=±5% resistance=330 package=THT]  # not connected
  R9 = Resistor [tolerance=±5% resistance=330 package=THT]  # not connected
  R10 = Resistor [tolerance=±5% resistance=330 package=THT]
  Argon3 = Particle Argon
  LED3 = RGB LED (com. cathode, rgb) [package="5 mm [THT]"]
  R11 = Resistor [tolerance=±5% resistance=10k package=THT]
  S4 = Magnetic Door Switch [package=reed_switch_plastic]
  R12 = TRIMPOT [package=3362u-2]

nets:
  N1: R6.Pin_0, LED3.red_anode
  N2: R6.Pin_1, Argon3.D3
  N3: R7.Pin_0, LED3.green_anode
  N4: R7.Pin_1, Argon3.D4
  N5: R10.Pin_0, LED3.blue_anode
  N6: R10.Pin_1, Argon3.D5
  N7: Argon3.3.3V, R11.Pin_0, R12.CCW
  N8: Argon3.GND, LED3.common_cathode, S4.2, R12.CW
  N9: Argon3.D2, R11.Pin_1, S4.1
  N10: Argon3.D6, R12.WIPER

custom parts:
  Particle Argon: The Argon is a powerful Wi-Fi enabled development board that can act as either a standalone Wi-Fi endpoint or Wi-Fi enabled gateway for Particle Mesh networks. It is based on the Nordic nRF52840 and has built-in battery charging circuitry so it’s easy to connect a Li-Po and deploy your local network in minutes. The Argon is great for connecting existing projects to the Particle Device Cloud or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
