# Fritzing sketch ble_health_temp (saved by Fritzing 0.9.3b)
breadboards: 1

parts:
  Argon1 = Particle Argon
  U1 = TMP36 [package=to-92-kit]

nets:
  3.3V: Argon1.3.3V, U1.VCC
  N1: Argon1.MD, U1.GND
  N2: Argon1.A3, U1.VOUT

custom parts:
  Particle Argon: The Argon is a powerful Wi-Fi enabled development board that can act as either a standalone Wi-Fi endpoint or Wi-Fi enabled gateway for Particle Mesh networks. It is based on the Nordic nRF52840 and has built-in battery charging circuitry so it’s easy to connect a Li-Po and deploy your local network in minutes. The Argon is great for connecting existing projects to the Particle Device Cloud or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
