# Fritzing sketch ble_uart_control (saved by Fritzing 0.9.3b)
breadboards: 1

parts:
  Argon1 = Particle Argon
  LED1 = RGB LED (com. cathode, rbg) [package="5 mm [THT]"]
  R1 = Resistor [tolerance=±5% resistance=220 package="1206 [SMD]"]
  R2 = Resistor [tolerance=±5% resistance=220 package="1206 [SMD]"]
  R3 = Resistor [tolerance=±5% resistance=220 package="1206 [SMD]"]
  U1 = TMP36 [package=to-92-kit]
  J1 = Piezo Speaker

nets:
  3.3V: Argon1.3.3V, U1.VCC
  N1: Argon1.MD, LED1.common_cathode, R1.Pin_1, R2.Pin_0, R2.Pin_1, R3.Pin_1, U1.GND, J1.pin1
  N2: Argon1.A0, LED1.green_anode, R3.Pin_0
  N3: Argon1.A1, LED1.blue_anode
  N4: Argon1.A2, LED1.red_anode, R1.Pin_0
  N5: Argon1.A3, U1.VOUT
  N6: Argon1.D6, J1.pin2

custom parts:
  Particle Argon: The Argon is a powerful Wi-Fi enabled development board that can act as either a standalone Wi-Fi endpoint or Wi-Fi enabled gateway for Particle Mesh networks. It is based on the Nordic nRF52840 and has built-in battery charging circuitry so it’s easy to connect a Li-Po and deploy your local network in minutes. The Argon is great for connecting existing projects to the Particle Device Cloud or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
