# Fritzing sketch i2c_lcd (saved by Fritzing 0.9.3b)
breadboards: 1

parts:
  LCD2 = LCD screen
  S1 = Pushbutton [package="[THT]"]
  Part6 = Adafruit I2C+SPI LCD Backpack [part_number="Adafruit #292"]
  R1 = Resistor [tolerance=±5% resistance=10k package="1206 [SMD]"]
  R2 = Resistor [tolerance=±5% resistance=4.7k package="1206 [SMD]"]
  R3 = Resistor [tolerance=±5% resistance=4.7k package="1206 [SMD]"]
  Argon1 = Particle Argon

nets:
  GND: LCD2.VSS, LCD2.R/W, Part6.GND, R1.Pin_0, Argon1.GND
  VDD: LCD2.VDD, LCD2.LED+, S1.Pin_1, S1.Pin_2, Part6.VCC, R2.Pin_1, R3.Pin_1, Argon1.VUSB
  N1: LCD2.V0, Part6.CONTRAST
  N2: LCD2.RS, Part6.RS
  N3: LCD2.E, Part6.E
  N4: LCD2.DB0, Part6.DB0
  N5: LCD2.DB1, Part6.DB1
  N6: LCD2.DB2, Part6.DB2
  N7: LCD2.DB3, Part6.DB3
  N8: LCD2.DB4, Part6.DB4
  N9: LCD2.DB5, Part6.DB5
  N10: LCD2.DB6, Part6.DB6
  N11: LCD2.DB7, Part6.DB7
  N12: LCD2.LED-, Part6.LEDK
  N13: S1.Pin_3, S1.Pin_4, R1.Pin_1, Argon1.D2
  N14: Part6.CLOCK, R3.Pin_0, Argon1.SCL
  N15: Part6.DATA, R2.Pin_0, Argon1.SDA

custom parts:
  Adafruit I2C+SPI LCD Backpack: LCD backpacks reduce the number of pins needed to connect to an LCD. LCDs are a fun and easy way to have your microcontroller project talk back to you. Character LCDs are common, and easy to get, available in tons of colors and sizes. We've written tutorials on using character LCDs with an Arduino (or similar microcontroller) but find that the number of pins necessary to control the LCD can be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
  Particle Argon: The Argon is a powerful Wi-Fi enabled development board that can act as either a standalone Wi-Fi endpoint or Wi-Fi enabled gateway for Particle Mesh networks. It is based on the Nordic nRF52840 and has built-in battery charging circuitry so it’s easy to connect a Li-Po and deploy your local network in minutes. The Argon is great for connecting existing projects to the Particle Device Cloud or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
