# Fritzing sketch pcb layout (saved by Fritzing 0.9.4)
circuit board: 5.97141cm x 5.6858cm
breadboards: 1

parts:
  LED1 = RGB LED - (4 legs) [package="5 mm [THT]"]
  LED2 = LED - 5mm [color="Red (633nm)" package="5 mm [THT]"]
  R1 = Resistor [tolerance=±5% resistance=220 package=THT]
  R2 = Resistor [tolerance=±5% resistance=220 package=THT]
  R3 = Resistor [tolerance=±5% resistance=220 package=THT]
  R4 = Resistor [tolerance=±5% resistance=220 package=THT]
  JP1 = Header 12 [package=1x12_machine-pin-header_lock.004]
  JP2 = M16 [package=1x16_machine-pin-header_lock.004]

nets:
  N1: LED1.red_cathode, R1.Pin_0
  N2: LED1.common_anode, LED2.cathode, JP2.4
  N3: LED1.green_cathode, R2.Pin_0
  N4: LED1.blue_cathode, R3.Pin_0
  N5: LED2.anode, R4.Pin_0
  N6: R1.Pin_1, JP1.10
  N7: R2.Pin_1, JP1.9
  N8: R3.Pin_1, JP1.8
  N9: R4.Pin_1, JP2.2
