# Fritzing sketch switch (saved by Fritzing 0.9.4)
breadboards: 1

parts:
  Argon2 = Particle Argon
  R3 = Resistor [tolerance=±5% resistance=330 package=THT]  # not connected
  R2 = Resistor [tolerance=±5% resistance=330 package=THT]  # not connected
  S1 = Toggle Switch [package=THT]

nets:
  N1: Argon2.3.3V, S1.L1
  N2: Argon2.GND, S1.L2
  N3: Argon2.D2, S1.COM

custom parts:
  Particle Argon: The Argon is a powerful Wi-Fi enabled development board that can act as either a standalone Wi-Fi endpoint or Wi-Fi enabled gateway for Particle Mesh networks. It is based on the Nordic nRF52840 and has built-in battery charging circuitry so it’s easy to connect a Li-Po and deploy your local network in minutes. The Argon is great for connecting existing projects to the Particle Device Cloud or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
