# Fritzing sketch photoresistor_and_potentiometer (saved by Fritzing 0.9.3b)
breadboards: 1

parts:
  R2 = Photocell (LDR) [package=THT]
  Argon1 = Particle Argon
  R3 = TRIMPOT [package=trimpot_pth_s3_lock]

nets:
  N1: R2.pin_0, Argon1.GND
  N2: R2.pin_1, Argon1.A0, R3.WIPER
  N3: Argon1.3.3V, R3.CW

custom parts:
  Particle Argon: The Argon is a powerful Wi-Fi enabled development board that can act as either a standalone Wi-Fi endpoint or Wi-Fi enabled gateway for Particle Mesh networks. It is based on the Nordic nRF52840 and has built-in battery charging circuitry so it’s easy to connect a Li-Po and deploy your local network in minutes. The Argon is great for connecting existing projects to the Particle Device Cloud or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
