# Fritzing sketch led (saved by Fritzing 0.9.10b)
breadboards: 1

parts:
  R1 = Resistor [tolerance=±5% resistance=330 power=0.25 package=THT]
  LED2 = LED - 5mm [color="Red (633nm)" current=0.030 package="5 mm [THT]"]
  A1 = Particle Photon 2

nets:
  N1: R1.Pin_0, LED2.anode
  N2: R1.Pin_1, A1.Pin_19
  N3: LED2.cathode, A1.Pin_4, A1.Pin_30
  N4: A1.Pin_28, A1.Pin_29

custom parts:
  Particle Photon 2: The Photon 2 is a development module with a microcontroller and Wi-Fi networking. -- This Fritzing file originally created by Peter Van Epp https://forum.fritzing.org/t/request-particle-photon2/19824/2 5/18/2024 - Rob Parke Rotated breadboard image
