# Fritzing sketch photoresistor_and_fixed_resistor_RGB_LED_schematic (saved by Fritzing 0.9.4)
circuit board: 8.46667cm x 5.64444cm
breadboards: 1

parts:
  Argon1 = Particle Argon
  R2 = Photocell (LDR) [package=THT]
  R8 = Resistor [tolerance=±5% resistance=330 package=THT]
  R6 = Resistor [tolerance=±5% resistance=330 package=THT]
  R7 = Resistor [tolerance=±5% resistance=330 package=THT]
  LED2 = RGB LED (com. cathode, rgb) [package="5 mm [THT]"]
  R3 = Resistor [tolerance=±5% resistance=4.7k package=THT]

nets:
  N1: Argon1.3.3V, R2.pin_0
  N2: Argon1.GND, R3.Pin_1
  N3: Argon1.A5, R2.pin_1, R3.Pin_0
  N4: Argon1.D2, R6.Pin_1
  N5: Argon1.D3, R7.Pin_1
  N6: Argon1.D4, R8.Pin_1
  N7: R8.Pin_0, LED2.blue_anode
  N8: R6.Pin_0, LED2.red_anode
  N9: R7.Pin_0, LED2.green_anode

custom parts:
  Particle Argon: The Argon is a powerful Wi-Fi enabled development board that can act as either a standalone Wi-Fi endpoint or Wi-Fi enabled gateway for Particle Mesh networks. It is based on the Nordic nRF52840 and has built-in battery charging circuitry so it’s easy to connect a Li-Po and deploy your local network in minutes. The Argon is great for connecting existing projects to the Particle Device Cloud or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
