# Fritzing sketch pot (saved by Fritzing 0.9.10b)
breadboards: 1

parts:
  R1 = TRIMPOT [maximum_resistance=10kΩ knob_status=50% power=0.5W package=3362u-2]
  A1 = Particle Photon 2

nets:
  N1: R1.CCW, A1.Pin_2
  N2: R1.WIPER, A1.Pin_5
  N3: R1.CW, A1.Pin_4, A1.Pin_30
  N4: A1.Pin_28, A1.Pin_29

custom parts:
  Particle Photon 2: The Photon 2 is a development module with a microcontroller and Wi-Fi networking. -- This Fritzing file originally created by Peter Van Epp https://forum.fritzing.org/t/request-particle-photon2/19824/2 5/18/2024 - Rob Parke Rotated breadboard image
