# Fritzing sketch correct_pullup_button_wiring (saved by Fritzing 0.9.4)
breadboards: 3

parts:
  R1 = Resistor [tolerance=±5% resistance=10k package=THT]
  S3 = Pushbutton [package="[THT]"]
  A1 = Particle Photon 2
  S4 = Pushbutton [package="[THT]"]
  A2 = Particle Photon 2
  S5 = Pushbutton [package="[THT]"]
  A3 = Particle Photon 2

nets:
  N1: R1.Pin_0, A3.Pin_2
  N2: R1.Pin_1, S5.Pin_3, S5.Pin_4, A3.Pin_19
  N3: S3.Pin_1, S3.Pin_2, A1.Pin_4, A1.Pin_30
  N4: S3.Pin_3, S3.Pin_4, A1.Pin_19
  N5: A1.Pin_28, A1.Pin_29
  N6: S4.Pin_1, S4.Pin_2, A2.Pin_4, A2.Pin_30
  N7: S4.Pin_3, S4.Pin_4, A2.Pin_2, A2.Pin_19, A2.Pin_31
  N8: A2.Pin_28, A2.Pin_29
  N9: S5.Pin_1, S5.Pin_2, A3.Pin_4, A3.Pin_30
  N10: A3.Pin_28, A3.Pin_29

custom parts:
  Particle Photon 2: The Photon 2 is a development module with a microcontroller and Wi-Fi networking. -- This Fritzing file originally created by Peter Van Epp https://forum.fritzing.org/t/request-particle-photon2/19824/2 5/18/2024 - Rob Parke Rotated breadboard image
