# Fritzing sketch rgb_led_common_anode (saved by Fritzing 0.9.4)
breadboards: 1

parts:
  R6 = Resistor [tolerance=±5% resistance=330 package=THT]
  R7 = Resistor [tolerance=±5% resistance=330 package=THT]
  R8 = Resistor [tolerance=±5% resistance=330 package=THT]  # not connected
  R9 = Resistor [tolerance=±5% resistance=330 package=THT]  # not connected
  R10 = Resistor [tolerance=±5% resistance=330 package=THT]
  LED2 = RGB LED (com. cathode, rgb) [package="5 mm [THT]"]
  Argon3 = Particle Argon

nets:
  N1: R6.Pin_0, LED2.red_anode
  N2: R6.Pin_1, Argon3.D2
  N3: R7.Pin_0, LED2.green_anode
  N4: R7.Pin_1, Argon3.D3
  N5: R10.Pin_0, LED2.blue_anode
  N6: R10.Pin_1, Argon3.D4

custom parts:
  Particle Argon: The Argon is a powerful Wi-Fi enabled development board that can act as either a standalone Wi-Fi endpoint or Wi-Fi enabled gateway for Particle Mesh networks. It is based on the Nordic nRF52840 and has built-in battery charging circuitry so it’s easy to connect a Li-Po and deploy your local network in minutes. The Argon is great for connecting existing projects to the Particle Device Cloud or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
