# Fritzing sketch rgb_led_common_cathode (saved by Fritzing 0.9.10b)
breadboards: 1

parts:
  R14 = Resistor [tolerance=±5% resistance=330 power=0.25 package=THT]
  R15 = Resistor [tolerance=±5% resistance=330 power=0.25 package=THT]
  R16 = Resistor [tolerance=±5% resistance=330 power=0.25 package=THT]
  LED4 = RGB LED (com. cathode, rgb) [package="5 mm [THT]"]
  A3 = Particle Photon 2

nets:
  N1: R14.Pin_0, LED4.red_anode
  N2: R14.Pin_1, A3.Pin_18
  N3: R15.Pin_0, LED4.green_anode
  N4: R15.Pin_1, A3.Pin_13
  N5: R16.Pin_0, LED4.blue_anode
  N6: R16.Pin_1, A3.Pin_12
  N7: LED4.common_cathode, A3.Pin_4, A3.Pin_30
  N8: A3.Pin_28, A3.Pin_29

custom parts:
  Particle Photon 2: The Photon 2 is a development module with a microcontroller and Wi-Fi networking. -- This Fritzing file originally created by Peter Van Epp https://forum.fritzing.org/t/request-particle-photon2/19824/2 5/18/2024 - Rob Parke Rotated breadboard image
