# Fritzing sketch rgb_led_pot (saved by Fritzing 0.9.10b)
breadboards: 1

parts:
  A3 = Particle Photon 2
  R10 = Resistor [tolerance=±5% resistance=330 power=0.25 package=THT]
  R11 = Resistor [tolerance=±5% resistance=330 power=0.25 package=THT]
  R12 = Resistor [tolerance=±5% resistance=330 power=0.25 package=THT]
  LED3 = RGB LED (com. cathode, rgb) [package="5 mm [THT]"]
  R13 = TRIMPOT [maximum_resistance=10kΩ knob_status=50% power=0.5W package=3362u-2]

nets:
  N1: A3.Pin_4, A3.Pin_30, LED3.common_cathode, R13.CCW
  N2: A3.Pin_5, R13.WIPER
  N3: A3.Pin_12, R12.Pin_1
  N4: A3.Pin_13, R11.Pin_1
  N5: A3.Pin_18, R10.Pin_1
  N6: A3.Pin_28, A3.Pin_29
  N7: R10.Pin_0, LED3.red_anode
  N8: R11.Pin_0, LED3.green_anode
  N9: R12.Pin_0, LED3.blue_anode

custom parts:
  Particle Photon 2: The Photon 2 is a development module with a microcontroller and Wi-Fi networking. -- This Fritzing file originally created by Peter Van Epp https://forum.fritzing.org/t/request-particle-photon2/19824/2 5/18/2024 - Rob Parke Rotated breadboard image
