# Fritzing sketch rgb_led_switch (saved by Fritzing 0.9.4)
breadboards: 1

parts:
  R1 = Resistor [tolerance=±5% resistance=330 package=THT]
  LED1 = RGB LED (com. cathode, rgb) [package="5 mm [THT]"]
  Argon2 = Particle Argon
  R4 = Resistor [tolerance=±5% resistance=330 package=THT]
  R5 = Resistor [tolerance=±5% resistance=330 package=THT]
  R3 = Resistor [tolerance=±5% resistance=330 package=THT]  # not connected
  R2 = Resistor [tolerance=±5% resistance=330 package=THT]  # not connected
  S1 = Toggle Switch [package=THT]

nets:
  N1: R1.Pin_0, LED1.red_anode
  N2: R1.Pin_1, Argon2.D2
  N3: LED1.green_anode, R4.Pin_0
  N4: LED1.blue_anode, R5.Pin_0
  N5: Argon2.3.3V, S1.L1
  N6: Argon2.GND, S1.L2
  N7: Argon2.A5, S1.COM
  N8: Argon2.D3, R4.Pin_1
  N9: Argon2.D4, R5.Pin_1

custom parts:
  Particle Argon: The Argon is a powerful Wi-Fi enabled development board that can act as either a standalone Wi-Fi endpoint or Wi-Fi enabled gateway for Particle Mesh networks. It is based on the Nordic nRF52840 and has built-in battery charging circuitry so it’s easy to connect a Li-Po and deploy your local network in minutes. The Argon is great for connecting existing projects to the Particle Device Cloud or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
