# Fritzing sketch photoresistor_without_fixed_resistor (saved by Fritzing 0.9.4)
breadboards: 1

parts:
  Argon1 = Particle Argon
  R2 = Photocell (LDR) [package=THT]

nets:
  N1: Argon1.3.3V, Argon1.A5, R2.pin_1
  N2: Argon1.GND, R2.pin_0

custom parts:
  Particle Argon: The Argon is a powerful Wi-Fi enabled development board that can act as either a standalone Wi-Fi endpoint or Wi-Fi enabled gateway for Particle Mesh networks. It is based on the Nordic nRF52840 and has built-in battery charging circuitry so it’s easy to connect a Li-Po and deploy your local network in minutes. The Argon is great for connecting existing projects to the Particle Device Cloud or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
