# Fritzing sketch tmp36 (saved by Fritzing 0.9.10b)
breadboards: 1

parts:
  U1 = TMP36 [package=to-92-kit]
  A1 = Particle Photon 2

nets:
  N1: U1.VCC, A1.Pin_2, A1.Pin_31
  N2: U1.VOUT, A1.Pin_8
  N3: U1.GND, A1.Pin_4, A1.Pin_30
  N4: A1.Pin_28, A1.Pin_29

custom parts:
  Particle Photon 2: The Photon 2 is a development module with a microcontroller and Wi-Fi networking. -- This Fritzing file originally created by Peter Van Epp https://forum.fritzing.org/t/request-particle-photon2/19824/2 5/18/2024 - Rob Parke Rotated breadboard image
