# Fritzing sketch stoplight_RGB_OLED (saved by Fritzing 0.9.4)
breadboards: 1

parts:
  Argon1 = Particle Argon
  R6 = Resistor [tolerance=±5% resistance=330 package=THT]
  LED2 = RGB LED (com. cathode, rgb) [package="5 mm [THT]"]
  R9 = Resistor [tolerance=±5% resistance=330 package=THT]
  R10 = Resistor [tolerance=±5% resistance=330 package=THT]
  R11 = Resistor [tolerance=±5% resistance=330 package=THT]
  LED3 = RGB LED (com. cathode, rgb) [package="5 mm [THT]"]
  R7 = Resistor [tolerance=±5% resistance=330 package=THT]
  R8 = Resistor [tolerance=±5% resistance=330 package=THT]
  Qwiic_OLED_Breakout3 = Qwiic_OLED_Breakout  # not connected

nets:
  N1: Argon1.GND, LED2.common_cathode, LED3.common_cathode
  N2: Argon1.A3, R11.Pin_1
  N3: Argon1.A4, R10.Pin_1
  N4: Argon1.A5, R9.Pin_1
  N5: Argon1.D2, R6.Pin_1
  N6: Argon1.D3, R7.Pin_1
  N7: Argon1.D4, R8.Pin_1
  N8: R6.Pin_0, LED2.red_anode
  N9: LED2.green_anode, R7.Pin_0
  N10: LED2.blue_anode, R8.Pin_0
  N11: R9.Pin_0, LED3.red_anode
  N12: R10.Pin_0, LED3.green_anode
  N13: R11.Pin_0, LED3.blue_anode

notes:
  North-South Signal
  West-East Signal
  Walk/Don't Walk
  use Qwiic cable

custom parts:
  Particle Argon: The Argon is a powerful Wi-Fi enabled development board that can act as either a standalone Wi-Fi endpoint or Wi-Fi enabled gateway for Particle Mesh networks. It is based on the Nordic nRF52840 and has built-in battery charging circuitry so it’s easy to connect a Li-Po and deploy your local network in minutes. The Argon is great for connecting existing projects to the Particle Device Cloud or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
  Qwiic_OLED_Breakout: The SparkFun Qwiic Micro OLED Breakout is a Qwiic-enabled version of our popular Micro OLED display! The small monochrome, blue-on-black OLED screen presents incredibly clear images for your viewing pleasure. It’s “micro,” but it still packs a punch --- the OLED display is crisp, and you can fit a deceivingly large amount of graphics on there. This breakout is perfect for adding graphics to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
