# Fritzing sketch servo_dc_fan_controller (saved by Fritzing 0.9.10b)
breadboards: 2

parts:
  Part1 = Motor Driver 1A Dual TB6612FNG  # not connected
  M1 = DC Motor [voltage_(max)=6V voltage_(min)=3V]  # not connected
  J2 = Basic Servo
  R1 = TRIMPOT [maximum_resistance=10kΩ knob_status=50% power=0.5W package=3362u-2]
  A1 = Particle Photon 2

nets:
  N1: J2.gnd, R1.CW, A1.Pin_4, A1.Pin_30, A1.Pin_32
  N2: J2.vcc, A1.Pin_26
  N3: J2.pulse, A1.Pin_7
  N4: R1.CCW, A1.Pin_2
  N5: R1.WIPER, A1.Pin_6
  N6: A1.Pin_28, A1.Pin_29

custom parts:
  Particle Photon 2: The Photon 2 is a development module with a microcontroller and Wi-Fi networking. -- This Fritzing file originally created by Peter Van Epp https://forum.fritzing.org/t/request-particle-photon2/19824/2 5/18/2024 - Rob Parke Rotated breadboard image
