# Fritzing sketch stoplight_RGB (saved by Fritzing 0.9.4)
breadboards: 2

parts:
  Argon1 = Particle Argon
  R6 = Resistor [tolerance=±5% resistance=330 package=THT]
  LED2 = RGB LED (com. cathode, rgb) [package="5 mm [THT]"]
  R9 = Resistor [tolerance=±5% resistance=330 package=THT]
  R10 = Resistor [tolerance=±5% resistance=330 package=THT]
  R11 = Resistor [tolerance=±5% resistance=330 package=THT]
  LED3 = RGB LED (com. cathode, rgb) [package="5 mm [THT]"]
  R13 = Resistor [tolerance=±5% resistance=330 package=THT]
  R14 = Resistor [tolerance=±5% resistance=330 package=THT]
  LED5 = LED - 5mm [color="Red (633nm)" package="5 mm [THT]"]
  LED6 = LED - 5mm [color="White (4500K)" package="5 mm [THT]"]
  R7 = Resistor [tolerance=±5% resistance=330 package=THT]
  R8 = Resistor [tolerance=±5% resistance=330 package=THT]

nets:
  N1: Argon1.GND, LED2.common_cathode, LED3.common_cathode, LED5.cathode, LED6.cathode
  N2: Argon1.A3, R11.Pin_1
  N3: Argon1.A4, R10.Pin_1
  N4: Argon1.A5, R9.Pin_1
  N5: Argon1.D2, R6.Pin_1
  N6: Argon1.D3, R7.Pin_1
  N7: Argon1.D4, R8.Pin_1
  N8: Argon1.D5, R13.Pin_1
  N9: Argon1.D6, R14.Pin_1
  N10: R6.Pin_0, LED2.red_anode
  N11: LED2.green_anode, R7.Pin_0
  N12: LED2.blue_anode, R8.Pin_0
  N13: R9.Pin_0, LED3.red_anode
  N14: R10.Pin_0, LED3.green_anode
  N15: R11.Pin_0, LED3.blue_anode
  N16: R13.Pin_0, LED5.anode
  N17: R14.Pin_0, LED6.anode

notes:
  North-South Signal
  West-East Signal
  Don't Walk Signal
  Walk Signal

custom parts:
  Particle Argon: The Argon is a powerful Wi-Fi enabled development board that can act as either a standalone Wi-Fi endpoint or Wi-Fi enabled gateway for Particle Mesh networks. It is based on the Nordic nRF52840 and has built-in battery charging circuitry so it’s easy to connect a Li-Po and deploy your local network in minutes. The Argon is great for connecting existing projects to the Particle Device Cloud or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
