# Fritzing sketch buzzer_and_RGB (saved by Fritzing 0.9.10b)
breadboards: 1

parts:
  A1 = Particle Photon 2
  J1 = Piezo Speaker
  LED1 = RGB LED (com. cathode, rgb) [package="5 mm [THT]"]
  R1 = Resistor [tolerance=±5% resistance=330 package="0603 [SMD]"]
  R2 = Resistor [tolerance=±5% resistance=330 package="0603 [SMD]"]
  R3 = Resistor [tolerance=±5% resistance=330 package="0603 [SMD]"]

nets:
  N1: A1.Pin_4, A1.Pin_30, A1.Pin_32, J1.pin1, LED1.common_cathode
  N2: A1.Pin_7, R1.Pin_1
  N3: A1.Pin_8, R2.Pin_1
  N4: A1.Pin_12, R3.Pin_1
  N5: A1.Pin_13, J1.pin2
  N6: A1.Pin_28, A1.Pin_29
  N7: LED1.red_anode, R1.Pin_0
  N8: LED1.green_anode, R2.Pin_0
  N9: LED1.blue_anode, R3.Pin_0

custom parts:
  Particle Photon 2: The Photon 2 is a development module with a microcontroller and Wi-Fi networking. -- This Fritzing file originally created by Peter Van Epp https://forum.fritzing.org/t/request-particle-photon2/19824/2 5/18/2024 - Rob Parke Rotated breadboard image
