# Fritzing sketch car (saved by Fritzing 0.9.10b)
breadboards: 1

parts:
  Part1 = Motor Driver 1A Dual TB6612FNG  # not connected
  M1 = DC Motor [voltage_(max)=6V voltage_(min)=3V]  # not connected
  M2 = DC Motor [voltage_(max)=6V voltage_(min)=3V]  # not connected
  U2 = LIPO-2000mAh [package=lipo-2000]
  J2 = JST-03JQ-BT [part_number=JST-JQ-BT package=THT]
  A1 = Particle Photon 2
  U3 = SWITCH_SPDT [package=kps-1290]

nets:
  N1: U2.+, J2.pin3
  N2: U2.-, J2.pin2
  N3: A1.Pin_4, A1.Pin_30, U3.S
  N4: A1.Pin_27, U3.P
  N5: A1.Pin_28, A1.Pin_29

notes:
  White LiPo connector plugs in to black Photon 2 battery port

custom parts:
  Particle Photon 2: The Photon 2 is a development module with a microcontroller and Wi-Fi networking. -- This Fritzing file originally created by Peter Van Epp https://forum.fritzing.org/t/request-particle-photon2/19824/2 5/18/2024 - Rob Parke Rotated breadboard image
