# Fritzing sketch car_lipo_hookup_no_wires (saved by Fritzing 0.9.4)
breadboards: 2

parts:
  Part1 = Motor Driver 1A Dual TB6612FNG
  Argon1 = Particle Argon
  M1 = DC Motor  # not connected
  M2 = DC Motor  # not connected
  U1 = SWITCH_SPDT [package=kps-1290]
  U2 = LIPO-2000mAh [package=lipo-2000]
  J2 = JST-03JQ-BT [part_number=JST-JQ-BT package=THT]

nets:
  N1: Part1.STBY, Argon1.3.3V
  N2: Argon1.GND, U1.S
  N3: Argon1.EN, U1.P
  N4: U2.+, J2.pin3
  N5: U2.-, J2.pin2

notes:
  White LiPo connector plugs in to black Argon battery port

custom parts:
  Particle Argon: The Argon is a powerful Wi-Fi enabled development board that can act as either a standalone Wi-Fi endpoint or Wi-Fi enabled gateway for Particle Mesh networks. It is based on the Nordic nRF52840 and has built-in battery charging circuitry so it’s easy to connect a Li-Po and deploy your local network in minutes. The Argon is great for connecting existing projects to the Particle Device Cloud or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
