# Fritzing sketch car_single_board (saved by Fritzing 0.9.10b)
breadboards: 1

parts:
  Part1 = Motor Driver 1A Dual TB6612FNG  # not connected
  Argon1 = Particle Argon
  M1 = DC Motor [voltage_(max)=6V voltage_(min)=3V]  # not connected
  M2 = DC Motor [voltage_(max)=6V voltage_(min)=3V]  # not connected
  U2 = LIPO-2000mAh [package=lipo-2000]
  J2 = JST-03JQ-BT [part_number=JST-JQ-BT package=THT]
  U3 = SWITCH_SPDT [package=kps-1290]

nets:
  N1: Argon1.GND, U3.S
  N2: Argon1.EN, U3.P
  N3: U2.+, J2.pin3
  N4: U2.-, J2.pin2

notes:
  White LiPo connector plugs in to black Argon battery port

custom parts:
  Particle Argon: The Argon is a powerful Wi-Fi enabled development board that can act as either a standalone Wi-Fi endpoint or Wi-Fi enabled gateway for Particle Mesh networks. It is based on the Nordic nRF52840 and has built-in battery charging circuitry so it’s easy to connect a Li-Po and deploy your local network in minutes. The Argon is great for connecting existing projects to the Particle Device Cloud or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
