# Fritzing sketch dcmotor (saved by Fritzing 0.9.10b)
breadboards: 1

parts:
  Part1 = Motor Driver 1A Dual TB6612FNG  # not connected
  M1 = DC Motor [voltage_(max)=6V voltage_(min)=3V]  # not connected
  A1 = Particle Photon 2

nets:
  N1: A1.Pin_4, A1.Pin_30
  N2: A1.Pin_28, A1.Pin_29

custom parts:
  Particle Photon 2: The Photon 2 is a development module with a microcontroller and Wi-Fi networking. -- This Fritzing file originally created by Peter Van Epp https://forum.fritzing.org/t/request-particle-photon2/19824/2 5/18/2024 - Rob Parke Rotated breadboard image
