# Fritzing sketch oled and ultrasonic (saved by Fritzing 0.9.4)
breadboards: 1

parts:
  Argon1 = Particle Argon
  SparkFun_Micro_OLED_Breakout1 = SparkFun Micro OLED Breakout [part_number=LCD-13003]  # not connected
  HC-SR04_Sensor_1 = HC-SR04 Ultrasonic Distance Sensor

nets:
  3.3V: Argon1.3.3V, HC-SR04_Sensor_1.VCC
  GND: Argon1.GND, HC-SR04_Sensor_1.GND
  N1: Argon1.D2, HC-SR04_Sensor_1.ECHO
  N2: Argon1.D3, HC-SR04_Sensor_1.TRIG

notes:
  GND -- GND
  3.3 -- 3.3V
  D1 -- MO
  D0 -- SCK
  D2 -- unused
  D/C -- A0
  RST -- A1
  CS -- A2

custom parts:
  Particle Argon: The Argon is a powerful Wi-Fi enabled development board that can act as either a standalone Wi-Fi endpoint or Wi-Fi enabled gateway for Particle Mesh networks. It is based on the Nordic nRF52840 and has built-in battery charging circuitry so it’s easy to connect a Li-Po and deploy your local network in minutes. The Argon is great for connecting existing projects to the Particle Device Cloud or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
  SparkFun Micro OLED Breakout: Description: The SparkFun Micro OLED Breakout Board breaks out a small monochrome, blue-on-black OLED. It’s “micro”, but it still packs a punch – the OLED display is crisp, and you can fit a deceivingly large amount of graphics on there. This breakout is perfect for adding graphics to your next Arduino project, displaying diagnostic information without resorting to serial output, and teaching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
