# Fritzing sketch servo_and_dc_motor (saved by Fritzing 0.9.10b)
breadboards: 1

parts:
  A2 = Particle Photon 2
  Part2 = Motor Driver 1A Dual TB6612FNG  # not connected
  J3 = Basic Servo
  M2 = DC Motor [voltage_(max)=6V voltage_(min)=3V]  # not connected

nets:
  N1: A2.Pin_4, A2.Pin_30, A2.Pin_32, J3.gnd
  N2: A2.Pin_7, J3.pulse
  N3: A2.Pin_26, J3.vcc
  N4: A2.Pin_28, A2.Pin_29

custom parts:
  Particle Photon 2: The Photon 2 is a development module with a microcontroller and Wi-Fi networking. -- This Fritzing file originally created by Peter Van Epp https://forum.fritzing.org/t/request-particle-photon2/19824/2 5/18/2024 - Rob Parke Rotated breadboard image
