# Fritzing sketch servo_and_dc_with_RGB (saved by Fritzing 0.9.10b)
breadboards: 2

parts:
  A3 = Particle Photon 2
  Part3 = Motor Driver 1A Dual TB6612FNG  # not connected
  J4 = Basic Servo
  M3 = DC Motor [voltage_(max)=6V voltage_(min)=3V]  # not connected
  LED1 = RGB LED (com. cathode, rgb) [package="5 mm [THT]"]
  R1 = Resistor [tolerance=±5% power=0.25 resistance=330 package=THT]
  R2 = Resistor [tolerance=±5% power=0.25 resistance=330 package=THT]
  R3 = Resistor [tolerance=±5% power=0.25 resistance=330 package=THT]

nets:
  N1: A3.Pin_4, A3.Pin_30, A3.Pin_32, J4.gnd, LED1.common_cathode
  N2: A3.Pin_7, J4.pulse
  N3: A3.Pin_12, R1.Pin_1
  N4: A3.Pin_13, R2.Pin_1
  N5: A3.Pin_18, R3.Pin_1
  N6: A3.Pin_26, J4.vcc
  N7: A3.Pin_28, A3.Pin_29
  N8: LED1.red_anode, R1.Pin_0
  N9: LED1.green_anode, R2.Pin_0
  N10: LED1.blue_anode, R3.Pin_0

custom parts:
  Particle Photon 2: The Photon 2 is a development module with a microcontroller and Wi-Fi networking. -- This Fritzing file originally created by Peter Van Epp https://forum.fritzing.org/t/request-particle-photon2/19824/2 5/18/2024 - Rob Parke Rotated breadboard image
