# Fritzing sketch ultrasonic (saved by Fritzing 0.9.4)
breadboards: 1

parts:
  Argon1 = Particle Argon
  HC-SR04_Sensor_1 = HC-SR04 Ultrasonic Distance Sensor

nets:
  GND: Argon1.GND, HC-SR04_Sensor_1.GND
  N1: Argon1.D5, HC-SR04_Sensor_1.ECHO
  N2: Argon1.D6, HC-SR04_Sensor_1.TRIG
  N3: Argon1.VUSB, HC-SR04_Sensor_1.VCC

custom parts:
  Particle Argon: The Argon is a powerful Wi-Fi enabled development board that can act as either a standalone Wi-Fi endpoint or Wi-Fi enabled gateway for Particle Mesh networks. It is based on the Nordic nRF52840 and has built-in battery charging circuitry so it’s easy to connect a Li-Po and deploy your local network in minutes. The Argon is great for connecting existing projects to the Particle Device Cloud or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
