# Fritzing sketch watch_with_switch (saved by Fritzing 0.9.4)
breadboards: 1

parts:
  SparkFun_Particle_Sensor_Breakout_-_MAX1 = SparkFun MAX30105_Breakout [part_number=SEN-14045]
  Argon3 = Particle Argon
  S4 = Pushbutton [package="[SMD]"]
  S5 = Toggle Switch [package=THT]
  R1 = Resistor [tolerance=±5% resistance=10k package="0603 [SMD]"]
  SparkFun_Micro_OLED_Breakout3 = SparkFun Micro OLED Breakout [part_number=LCD-13003]  # not connected

nets:
  N1: SparkFun_Particle_Sensor_Breakout_-_MAX1.SCL, Argon3.SCL
  N2: SparkFun_Particle_Sensor_Breakout_-_MAX1.SDA, Argon3.SDA
  5V: SparkFun_Particle_Sensor_Breakout_-_MAX1.5V, Argon3.3.3V, R1.Pin_1
  GND: SparkFun_Particle_Sensor_Breakout_-_MAX1.GND, Argon3.GND, S5.L2
  N3: Argon3.D3, S4.Pin_1, S4.Pin_2
  N4: Argon3.EN, S5.COM

notes:
  Use Qwiic cable

custom parts:
  SparkFun MAX30105_Breakout: Description: The SparkFun MAX30105 Particle Sensor is a flexible, powerful sensor enabling sensing of distance, heart rate, particle detection and even the blinking of an eye. The MAX30105 has been equipped with three LEDs as well as a very sensitive photon detector. The idea is to pulse the different LEDs, then detect what shines back. Based on the reflected signature it’s possible to detect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
  Particle Argon: The Argon is a powerful Wi-Fi enabled development board that can act as either a standalone Wi-Fi endpoint or Wi-Fi enabled gateway for Particle Mesh networks. It is based on the Nordic nRF52840 and has built-in battery charging circuitry so it’s easy to connect a Li-Po and deploy your local network in minutes. The Argon is great for connecting existing projects to the Particle Device Cloud or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
  SparkFun Micro OLED Breakout: Description: The SparkFun Micro OLED Breakout Board breaks out a small monochrome, blue-on-black OLED. It’s “micro”, but it still packs a punch – the OLED display is crisp, and you can fit a deceivingly large amount of graphics on there. This breakout is perfect for adding graphics to your next Arduino project, displaying diagnostic information without resorting to serial output, and teaching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
