# Fritzing sketch accelerometer (saved by Fritzing 0.9.3b)
breadboards: 1

parts:
  Argon1 = Particle Argon
  3-Axis_Accelerometer2 = 3-Axis Accelerometer Breakout - MMA8452Q

nets:
  3.3V: Argon1.3.3V, 3-Axis_Accelerometer2.3.3V
  GND: Argon1.GND, 3-Axis_Accelerometer2.GND
  N1: Argon1.SDA, 3-Axis_Accelerometer2.SDA
  N2: Argon1.SCL, 3-Axis_Accelerometer2.SCL

custom parts:
  Particle Argon: The Argon is a powerful Wi-Fi enabled development board that can act as either a standalone Wi-Fi endpoint or Wi-Fi enabled gateway for Particle Mesh networks. It is based on the Nordic nRF52840 and has built-in battery charging circuitry so it’s easy to connect a Li-Po and deploy your local network in minutes. The Argon is great for connecting existing projects to the Particle Device Cloud or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
