# Fritzing sketch accelerometer_rgb_led (saved by Fritzing 0.9.10b)
breadboards: 1

parts:
  R9 = Resistor [tolerance=±5% resistance=330 power=0.25 package=THT]
  R10 = Resistor [tolerance=±5% resistance=330 power=0.25 package=THT]
  R11 = Resistor [tolerance=±5% resistance=330 power=0.25 package=THT]
  LED3 = RGB LED (com. cathode, rgb) [package="5 mm [THT]"]
  Part1 = Triple Axis Accelerometer Breakout - ADXL345
  A1 = Particle Photon 2

nets:
  N1: R9.Pin_0, LED3.red_anode
  N2: R9.Pin_1, A1.Pin_7
  N3: R10.Pin_0, LED3.green_anode
  N4: R10.Pin_1, A1.Pin_8
  N5: R11.Pin_0, LED3.blue_anode
  N6: R11.Pin_1, A1.Pin_12
  N7: LED3.common_cathode, Part1.GND, Part1.SDO, A1.Pin_4, A1.Pin_30
  N8: Part1.VCC, Part1.CS, A1.Pin_2
  N9: Part1.SDA, A1.Pin_17
  N10: Part1.SCL, A1.Pin_18
  N11: A1.Pin_28, A1.Pin_29

custom parts:
  Particle Photon 2: The Photon 2 is a development module with a microcontroller and Wi-Fi networking. -- This Fritzing file originally created by Peter Van Epp https://forum.fritzing.org/t/request-particle-photon2/19824/2 5/18/2024 - Rob Parke Rotated breadboard image
