# Fritzing sketch pir_sparkfun (saved by Fritzing 0.9.3b)
breadboards: 1

parts:
  Part7 = HC-SR501 Body Sensor Module
  Argon1 = Particle Argon
  R1 = Resistor [tolerance=±5% resistance=10k package="2010 [SMD]"]

nets:
  N1: Part7.VCC, Argon1.D2, R1.Pin_1
  N2: Part7.GND, Argon1.VUSB, R1.Pin_0

notes:
  Note Sparkfun PIR wiring

custom parts:
  HC-SR501 Body Sensor Module: Pyroelectric Infrared PIR Motion Sensor Detector Module
  Particle Argon: The Argon is a powerful Wi-Fi enabled development board that can act as either a standalone Wi-Fi endpoint or Wi-Fi enabled gateway for Particle Mesh networks. It is based on the Nordic nRF52840 and has built-in battery charging circuitry so it’s easy to connect a Li-Po and deploy your local network in minutes. The Argon is great for connecting existing projects to the Particle Device Cloud or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
