# Fritzing sketch rfid (saved by Fritzing 0.9.4)
breadboards: 1

parts:
  Argon1 = Particle Argon
  Part1 = RFID-RC522-v2

nets:
  3.3V: Argon1.3.3V, Part1.3.3V
  GND: Argon1.GND, Part1.GND
  N1: Argon1.A4, Part1.SDA
  N2: Argon1.A5, Part1.RST
  N3: Argon1.SCK, Part1.SCK
  N4: Argon1.MO, Part1.MOSI
  N5: Argon1.MI, Part1.MISO

custom parts:
  Particle Argon: The Argon is a powerful Wi-Fi enabled development board that can act as either a standalone Wi-Fi endpoint or Wi-Fi enabled gateway for Particle Mesh networks. It is based on the Nordic nRF52840 and has built-in battery charging circuitry so it’s easy to connect a Li-Po and deploy your local network in minutes. The Argon is great for connecting existing projects to the Particle Device Cloud or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
  RFID-RC522-v2: A simple China made RFID-RC522 Reader; do check the pin labels, as this is a MFRC522 based clone.
