# Fritzing sketch pcb_layout_example_ic (saved by Fritzing 0.9.4)
breadboards: 1

parts:
  Argon1 = Particle Argon
  S1 = Momentary Switch [package=ksa_sealed_tac_switch]
  R1 = Resistor [tolerance=±5% resistance=10k package=THT]
  LED1 = smd LED [color="Red (633nm)" package="0805 [SMD]"]
  R3 = Resistor [tolerance=±5% resistance=330 package=THT]

nets:
  N1: Argon1.3.3V, R1.Pin_1
  N2: Argon1.GND, S1.2, R3.Pin_1
  N3: Argon1.D2, LED1.anode
  N4: Argon1.D8, S1.3
  N5: S1.4, R1.Pin_0
  N6: LED1.cathode, R3.Pin_0

custom parts:
  Particle Argon: The Argon is a powerful Wi-Fi enabled development board that can act as either a standalone Wi-Fi endpoint or Wi-Fi enabled gateway for Particle Mesh networks. It is based on the Nordic nRF52840 and has built-in battery charging circuitry so it’s easy to connect a Li-Po and deploy your local network in minutes. The Argon is great for connecting existing projects to the Particle Device Cloud or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
