# Fritzing sketch rgb_led_common_cathode (saved by Fritzing 0.9.3b)
breadboards: 1

parts:
  R1 = Resistor [tolerance=±5% resistance=330 package=THT]
  LED1 = RGB LED (com. cathode, rgb) [package="5 mm [THT]"]
  Argon1 = Particle Argon

nets:
  N1: R1.Pin_0, Argon1.D3
  N2: R1.Pin_1, LED1.red_anode
  N3: LED1.common_cathode, Argon1.GND

custom parts:
  Particle Argon: The Argon is a powerful Wi-Fi enabled development board that can act as either a standalone Wi-Fi endpoint or Wi-Fi enabled gateway for Particle Mesh networks. It is based on the Nordic nRF52840 and has built-in battery charging circuitry so it’s easy to connect a Li-Po and deploy your local network in minutes. The Argon is great for connecting existing projects to the Particle Device Cloud or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
