# Fritzing sketch rgb_led_tmp36 (saved by Fritzing 0.9.10b)
breadboards: 1

parts:
  R1 = Resistor [tolerance=±5% resistance=330 power=0.25 package=THT]
  LED1 = RGB LED (com. cathode, rgb) [package="5 mm [THT]"]
  R4 = Resistor [tolerance=±5% resistance=330 power=0.25 package=THT]
  R5 = Resistor [tolerance=±5% resistance=330 power=0.25 package=THT]
  U1 = TMP36 [package=to-92-kit]
  A1 = Particle Photon 2

nets:
  N1: R1.Pin_0, LED1.red_anode
  N2: R1.Pin_1, A1.Pin_7
  N3: LED1.green_anode, R4.Pin_0
  N4: LED1.blue_anode, R5.Pin_0
  N5: R4.Pin_1, A1.Pin_8
  N6: R5.Pin_1, A1.Pin_12
  N7: U1.VCC, A1.Pin_2, A1.Pin_31
  N8: U1.VOUT, A1.Pin_5
  N9: U1.GND, A1.Pin_4, A1.Pin_30
  N10: A1.Pin_28, A1.Pin_29

custom parts:
  Particle Photon 2: The Photon 2 is a development module with a microcontroller and Wi-Fi networking. -- This Fritzing file originally created by Peter Van Epp https://forum.fritzing.org/t/request-particle-photon2/19824/2 5/18/2024 - Rob Parke Rotated breadboard image
