# Fritzing sketch tmp36 (saved by Fritzing 0.9.4)
breadboards: 1

parts:
  Argon2 = Particle Argon
  R2 = Resistor [tolerance=±5% resistance=330 package=THT]  # not connected
  R3 = Resistor [tolerance=±5% resistance=330 package=THT]  # not connected
  U1 = TMP36 [package=to-92-kit]

nets:
  3.3V: Argon2.3.3V, U1.VCC
  GND: Argon2.GND, U1.GND
  N1: Argon2.A5, U1.VOUT

custom parts:
  Particle Argon: The Argon is a powerful Wi-Fi enabled development board that can act as either a standalone Wi-Fi endpoint or Wi-Fi enabled gateway for Particle Mesh networks. It is based on the Nordic nRF52840 and has built-in battery charging circuitry so it’s easy to connect a Li-Po and deploy your local network in minutes. The Argon is great for connecting existing projects to the Particle Device Cloud or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
